// Logisim project project2.circ as structural Verilog: 2 circuits, main circuit main
module main (
  output [7:0] out_1,
  output [7:0] out_2,
  output [7:0] out_3,
  output [7:0] out_4
);

  wire and_1_out, clock_1_out, not_1_out;
  wire [1:0] InstructionMemory_dout, InstructionMemory_dout_2, InstructionMemory_dout_3,
       InstructionMemory_dout_4;
  wire [7:0] adder_1_out, adder_2_out, multiplexer_2_out, PC_q, registerfile_1_regdata1,
       registerfile_1_regdata2, subtractor_1_out;

  Adder adder_1 (.a(PC_q), .b(8'h1), .out(adder_1_out));  // open: cin, cout
  Clock clock_1 (.out(clock_1_out));
  Register PC (.D(adder_1_out), .clk(clock_1_out), .Q(PC_q));  // open: en, clr
  and and_1 (and_1_out, InstructionMemory_dout_4[0], InstructionMemory_dout_4[1]);
  Hex_Digit_Display baba (.value(PC_q[7:4]));  // open: dp
  Hex_Digit_Display baba_1 (.value(PC_q[3:0]));  // open: dp
  not not_1 (not_1_out, and_1_out);
  RAM #(.enables("line")) InstructionMemory (
    .addr(PC_q), .clk(clock_1_out),
    .dout({InstructionMemory_dout_4, InstructionMemory_dout_3, InstructionMemory_dout_2, InstructionMemory_dout}));  // open: we, din
  registerfile registerfile_1 (
    .WriteReg(InstructionMemory_dout_3), .ReadReg1(InstructionMemory_dout_2), .RegDataW(multiplexer_2_out),
    .WriteEnable(not_1_out), .ReadReg2(InstructionMemory_dout), .TheClock(clock_1_out),
    .RegData1(registerfile_1_regdata1), .RegData2(registerfile_1_regdata2));
  Adder adder_2 (.a(registerfile_1_regdata1), .b(registerfile_1_regdata2), .out(adder_2_out));  // open: cin, cout
  Subtractor subtractor_1 (
    .a(registerfile_1_regdata1), .b(registerfile_1_regdata2), .out(subtractor_1_out));  // open: bin, bout
  Multiplexer #(.select(2), .width(8)) multiplexer_1 (
    .in0(adder_2_out), .in1(subtractor_1_out), .in2(adder_2_out), .in3(adder_2_out), .out(out_1),
    .sel(InstructionMemory_dout_4));
  RAM #(.enables("line")) DataMemory (
    .addr(out_1), .we(and_1_out), .clk(clock_1_out), .din(registerfile_1_regdata1), .dout(out_3));
  Multiplexer #(.width(8)) multiplexer_2 (
    .in0(out_1), .in1(out_3), .out(multiplexer_2_out), .sel(InstructionMemory_dout_4[1]));

  assign out_2 = out_1;
  assign out_4 = out_3;

  // Notes on the sheet:
  //   ProgramCounter
  //   CPU: yo
  //   Brandon Gaona and Zidan Kazi
  //   I pledge my honor that I have abided by the Stevens Honor System.
  //   ALU
endmodule

module registerfile (
  input  [1:0] WriteReg,
  input  [1:0] ReadReg1,
  input  [7:0] RegDataW,
  input  WriteEnable,
  input  [1:0] ReadReg2,
  input  TheClock,
  output [7:0] RegData1,
  output [7:0] RegData2
);

  wire and_1_out, and_2_out, and_3_out, and_4_out, decoder_1_out0, decoder_1_out1, decoder_1_out2,
       decoder_1_out3;
  wire [7:0] X0_q, X1_q, X2_q, X3_q;

  Decoder #(.select(2)) decoder_1 (
    .out0(decoder_1_out0), .out1(decoder_1_out1), .out2(decoder_1_out2), .out3(decoder_1_out3), .sel(WriteReg));  // open: en
  and and_1 (and_1_out, WriteEnable, decoder_1_out0);
  and and_2 (and_2_out, WriteEnable, decoder_1_out1);
  and and_3 (and_3_out, WriteEnable, decoder_1_out2);
  and and_4 (and_4_out, WriteEnable, decoder_1_out3);
  Register X0 (.D(RegDataW), .en(and_1_out), .clk(TheClock), .Q(X0_q));  // open: clr
  Register X1 (.D(RegDataW), .en(and_2_out), .clk(TheClock), .Q(X1_q));  // open: clr
  Register X2 (.D(RegDataW), .en(and_3_out), .clk(TheClock), .Q(X2_q));  // open: clr
  Register X3 (.D(RegDataW), .en(and_4_out), .clk(TheClock), .Q(X3_q));  // open: clr
  // Probe on X0_q
  // Probe on X1_q
  // Probe on X2_q
  // Probe on X3_q
  Multiplexer #(.select(2), .width(8)) multiplexer_1 (
    .in0(X0_q), .in1(X1_q), .in2(X2_q), .in3(X3_q), .out(RegData1), .sel(ReadReg1));
  Multiplexer #(.select(2), .width(8)) multiplexer_2 (
    .in0(X0_q), .in1(X1_q), .in2(X2_q), .in3(X3_q), .out(RegData2), .sel(ReadReg2));
endmodule
